// Digital circuit ALU.dig as structural Verilog
module ALU (
  input  Esquerda_Direita,
  input  in_2,
  input  in_3,
  input  in_4,
  input  [7:0] B,
  input  [7:0] A,
  input  Shift_Left__Rigth,
  input  [7:0] in_9,
  output out_7,
  output out_10
);

  wire [7:0] and8bits_1_s, multiplexer_1_out, multiplicador4bits_1_s, or8bits_1_s, shiftleftright_1_s,
       somador8bits_1_s, subtrator8bits_1_s, xor8bits_1_p3;

  somador8bits somador8bits_1 (.A(A), .B(B), .OVERFLOW(out_7), .S(somador8bits_1_s));
  Subtrator8bits subtrator8bits_1 (.A(A), .B(B), .OVERFLOW(out_10), .S(subtrator8bits_1_s));
  AND8bits and8bits_1 (.A(A), .B(B), .S(and8bits_1_s));
  // xor8bits xor8bits_1: pin names not known; wires that end beside it: A, B, xor8bits_1_p3
  Or8bits or8bits_1 (.A(A), .B(B), .S(or8bits_1_s));
  shiftLeftRight shiftleftright_1 (.Direita_Esquerda(Shift_Left__Rigth), .E(B), .S(shiftleftright_1_s));
  Multiplicador4bits multiplicador4bits_1 (.B(A[3:0]), .A(B[3:0]), .S(multiplicador4bits_1_s));
  Multiplexer #(.Selector_Bits(3), .Bits(8)) multiplexer_1 (
    .sel({in_4, in_2, in_3}), .in_0(somador8bits_1_s), .in_1(subtrator8bits_1_s), .in_2(and8bits_1_s),
    .in_3(xor8bits_1_p3), .in_4(or8bits_1_s), .in_5(shiftleftright_1_s), .in_6(multiplicador4bits_1_s),
    .in_7(in_9), .out(multiplexer_1_out));
  Seven_Seg_Hex seven_seg_hex_1 (.d(multiplexer_1_out[7:4]), .dp(1'b0));
  Seven_Seg_Hex seven_seg_hex_2 (.d(multiplexer_1_out[3:0]), .dp(1'b0));
endmodule
