// Digital circuit Multiplicador4bits.dig as structural Verilog
module Multiplicador4bits (
  input  [3:0] B,
  input  [3:0] A,
  output [7:0] S
);

  wire and_1_out, and_2_out, and_3_out, and_4_out, and_5_out, and_6_out, and_7_out, and_8_out, and_9_out,
       and_10_out, and_11_out, and_12_out, and_13_out, and_14_out, and_15_out, meiosomador_1_v,
       meiosomador_2_v, meiosomador_3_v, meiosomador_4_v, somador_1_bit_2_so, somador_1_bit_2_v,
       somador_1_bit_3_v, somador_1_bit_4_so, somador_1_bit_4_v, somador_1_bit_5_so, somador_1_bit_5_v,
       somador_1_bit_6_so, somador_1_bit_6_v, somador_1_bit_7_so, somador_1_bit_7_v, somador_1_bit_8_so,
       somador_1_bit_8_v;

  and and_1 (and_1_out, B[3], A[3]);
  Somador_1_bit somador_1_bit_1 (.B(somador_1_bit_3_v), .A(somador_1_bit_2_v), .C(and_1_out), .So(S[6]), .V(S[7]));
  and and_2 (and_2_out, B[3], A[2]);
  and and_3 (and_3_out, B[2], A[3]);
  Somador_1_bit somador_1_bit_2 (
    .B(somador_1_bit_5_v), .A(and_3_out), .C(and_2_out), .So(somador_1_bit_2_so), .V(somador_1_bit_2_v));
  Somador_1_bit somador_1_bit_3 (
    .B(meiosomador_1_v), .A(somador_1_bit_4_v), .C(somador_1_bit_2_so), .So(S[5]), .V(somador_1_bit_3_v));
  and and_4 (and_4_out, B[3], A[1]);
  Somador_1_bit somador_1_bit_4 (
    .B(somador_1_bit_6_v), .A(somador_1_bit_5_so), .C(and_4_out), .So(somador_1_bit_4_so),
    .V(somador_1_bit_4_v));
  and and_5 (and_5_out, B[2], A[2]);
  Somador_1_bit somador_1_bit_5 (
    .B(somador_1_bit_7_v), .A(and_6_out), .C(and_5_out), .So(somador_1_bit_5_so), .V(somador_1_bit_5_v));
  meioSomador meiosomador_1 (.B(somador_1_bit_4_so), .A(meiosomador_2_v), .So(S[4]), .V(meiosomador_1_v));
  and and_6 (and_6_out, B[1], A[3]);
  and and_7 (and_7_out, B[3], A[0]);
  and and_8 (and_8_out, B[2], A[1]);
  Somador_1_bit somador_1_bit_6 (
    .B(meiosomador_3_v), .A(and_8_out), .C(somador_1_bit_7_so), .So(somador_1_bit_6_so), .V(somador_1_bit_6_v));
  and and_9 (and_9_out, B[1], A[2]);
  and and_10 (and_10_out, B[0], A[3]);
  Somador_1_bit somador_1_bit_7 (
    .B(somador_1_bit_8_v), .A(and_10_out), .C(and_9_out), .So(somador_1_bit_7_so), .V(somador_1_bit_7_v));
  meioSomador meiosomador_2 (.B(somador_1_bit_6_so), .A(and_7_out), .So(S[3]), .V(meiosomador_2_v));
  and and_11 (and_11_out, B[2], A[0]);
  and and_12 (and_12_out, B[1], A[1]);
  meioSomador meiosomador_3 (.B(somador_1_bit_8_so), .A(and_11_out), .So(S[2]), .V(meiosomador_3_v));
  Somador_1_bit somador_1_bit_8 (
    .B(meiosomador_4_v), .A(and_13_out), .C(and_12_out), .So(somador_1_bit_8_so), .V(somador_1_bit_8_v));
  and and_13 (and_13_out, B[0], A[2]);
  and and_14 (and_14_out, B[1], A[0]);
  meioSomador meiosomador_4 (.B(and_15_out), .A(and_14_out), .So(S[1]), .V(meiosomador_4_v));
  and and_15 (and_15_out, B[0], A[1]);
  and and_16 (S[0], B[0], A[0]);
endmodule
