// Digital circuit Somador 1 bit.dig as structural Verilog
module Somador_1_bit (
  input  B,
  input  A,
  input  C,
  output So,
  output V
);

  wire and_1_out, and_2_out, and_3_out, xor_1_out;

  xor xor_1 (xor_1_out, A, B);
  and and_1 (and_1_out, C, B);
  and and_2 (and_2_out, A, C);
  and and_3 (and_3_out, A, B);
  xor xor_2 (So, xor_1_out, C);
  or or_1 (V, and_1_out, and_2_out, and_3_out);
endmodule
