// Digital circuit Subtrator8bits.dig as structural Verilog
module Subtrator8bits (
  input  [7:0] A,
  input  [7:0] B,
  output OVERFLOW,
  output [7:0] S
);

  wire subtrator1bit_2_ts, subtrator1bit_3_ts, subtrator1bit_4_ts, subtrator1bit_5_ts, subtrator1bit_6_ts,
       subtrator1bit_7_ts, subtrator1bit_8_ts;

  subtrator1bit subtrator1bit_1 (.B(B[7]), .A(A[7]), .C(subtrator1bit_2_ts), .Sb(S[7]), .Ts(OVERFLOW));
  subtrator1bit subtrator1bit_2 (.B(B[6]), .A(A[6]), .C(subtrator1bit_3_ts), .Sb(S[6]), .Ts(subtrator1bit_2_ts));
  subtrator1bit subtrator1bit_3 (.B(B[5]), .A(A[5]), .C(subtrator1bit_4_ts), .Sb(S[5]), .Ts(subtrator1bit_3_ts));
  subtrator1bit subtrator1bit_4 (.B(B[4]), .A(A[4]), .C(subtrator1bit_5_ts), .Sb(S[4]), .Ts(subtrator1bit_4_ts));
  subtrator1bit subtrator1bit_5 (.B(B[3]), .A(A[3]), .C(subtrator1bit_6_ts), .Sb(S[3]), .Ts(subtrator1bit_5_ts));
  subtrator1bit subtrator1bit_6 (.B(B[2]), .A(A[2]), .C(subtrator1bit_7_ts), .Sb(S[2]), .Ts(subtrator1bit_6_ts));
  subtrator1bit subtrator1bit_7 (.B(B[1]), .A(A[1]), .C(subtrator1bit_8_ts), .Sb(S[1]), .Ts(subtrator1bit_7_ts));
  subtrator1bit subtrator1bit_8 (.B(B[0]), .A(A[0]), .C(1'b0), .Sb(S[0]), .Ts(subtrator1bit_8_ts));
endmodule
