// Digital circuit Subtrator8bitsDisplay.dig as structural Verilog
module Subtrator8bitsDisplay (
  input  in_1,
  input  in_2,
  input  in_3,
  input  in_4,
  input  in_5,
  input  in_6,
  input  in_7,
  input  in_8,
  input  in_9,
  input  in_10,
  input  in_11,
  input  in_12,
  input  in_13,
  input  in_14,
  input  in_15,
  input  in_16,
  output Overflow
);

  wire subtrator1bit_2_ts, subtrator1bit_3_ts, subtrator1bit_4_ts, subtrator1bit_5_ts, subtrator1bit_6_ts,
       subtrator1bit_7_ts, subtrator1bit_8_ts;
  wire [3:0] subtrator1bit_4_sb, subtrator1bit_5_sb;

  subtrator1bit subtrator1bit_1 (
    .B(in_10), .A(in_2), .C(subtrator1bit_2_ts), .Sb(subtrator1bit_4_sb[3]), .Ts(Overflow));
  subtrator1bit subtrator1bit_2 (
    .B(in_9), .A(in_1), .C(subtrator1bit_3_ts), .Sb(subtrator1bit_4_sb[2]), .Ts(subtrator1bit_2_ts));
  subtrator1bit subtrator1bit_3 (
    .B(in_11), .A(in_3), .C(subtrator1bit_4_ts), .Sb(subtrator1bit_4_sb[1]), .Ts(subtrator1bit_3_ts));
  subtrator1bit subtrator1bit_4 (
    .B(in_15), .A(in_7), .C(subtrator1bit_5_ts), .Sb(subtrator1bit_4_sb[0]), .Ts(subtrator1bit_4_ts));
  Seven_Seg_Hex seven_seg_hex_1 (.d(subtrator1bit_4_sb), .dp(1'b0));
  Seven_Seg_Hex seven_seg_hex_2 (.d(subtrator1bit_5_sb), .dp(1'b0));
  subtrator1bit subtrator1bit_5 (
    .B(in_16), .A(in_8), .C(subtrator1bit_6_ts), .Sb(subtrator1bit_5_sb[2]), .Ts(subtrator1bit_5_ts));
  subtrator1bit subtrator1bit_6 (
    .B(in_13), .A(in_5), .C(subtrator1bit_7_ts), .Sb(subtrator1bit_5_sb[3]), .Ts(subtrator1bit_6_ts));
  subtrator1bit subtrator1bit_7 (
    .B(in_12), .A(in_4), .C(subtrator1bit_8_ts), .Sb(subtrator1bit_5_sb[1]), .Ts(subtrator1bit_7_ts));
  subtrator1bit subtrator1bit_8 (.B(in_14), .A(in_6), .C(1'b0), .Sb(subtrator1bit_5_sb[0]), .Ts(subtrator1bit_8_ts));
endmodule
