// Digital circuit alu.dig as structural Verilog
module alu (
  input  [11:0] in_1,
  input  in_2,
  input  in_3,
  input  [2:0] in_4,
  input  [7:0] in_5
);

  wire aluc_1_of, aluc_1_of2, Clock;
  wire [3:0] register_1_q;
  wire [7:0] aluc_1__0_7;
  wire [7:4] register_1_q_2;
  wire [11:0] eepromdualport_1_d;

  Button button_1 (.out(Clock));
  EEPROMDualPort #(.AddrBits(3), .Bits(12)) eepromdualport_1 (
    .A(in_4), .Din(in_1), .str(in_2), .C(Clock), .ld(1'b1), .D(eepromdualport_1_d));
  ALUc aluc_1 (
    .B2(eepromdualport_1_d[9]), .B1(eepromdualport_1_d[8]), .B3(eepromdualport_1_d[10]),
    .B(eepromdualport_1_d[7:0]), .A({register_1_q_2, register_1_q}), .Shift_Left__Rigth(in_3), .ndaa(in_5),
    .nda(in_5), .Of(aluc_1_of), ._0_7(aluc_1__0_7), .Of2(aluc_1_of2));
  LED led_1 (.in(aluc_1_of));
  LED led_2 (.in(aluc_1_of2));
  Register #(.Bits(8)) register_1 (.D(aluc_1__0_7), .C(Clock), .en(1'b1), .Q({register_1_q_2, register_1_q}));
  Seven_Seg_Hex seven_seg_hex_1 (.d(register_1_q_2), .dp(1'b0));
  Seven_Seg_Hex seven_seg_hex_2 (.d(register_1_q), .dp(1'b0));

  // Notes on the sheet:
  //   contents of eepromdualport_1 (hex, n*v repeats v):
  //   0,1,8,0,0,a
endmodule
