// Digital circuit shiftLeftRight.dig as structural Verilog
module shiftLeftRight (
  input  Direita_Esquerda,
  input  [7:0] E,
  output [7:0] S
);

  wire and_1_out, and_3_out, and_4_out, and_5_out, and_6_out, and_7_out, and_8_out, and_9_out, and_10_out,
       and_11_out, and_12_out, and_14_out, not_1_out;

  not not_1 (not_1_out, Direita_Esquerda);
  and and_1 (and_1_out, Direita_Esquerda, E[7]);
  and and_2 (S[7], E[6], not_1_out);
  and and_3 (and_3_out, Direita_Esquerda, E[6]);
  or or_1 (S[6], and_4_out, and_1_out);
  and and_4 (and_4_out, E[5], not_1_out);
  and and_5 (and_5_out, Direita_Esquerda, E[5]);
  or or_2 (S[5], and_6_out, and_3_out);
  and and_6 (and_6_out, E[4], not_1_out);
  or or_3 (S[4], and_8_out, and_5_out);
  and and_7 (and_7_out, Direita_Esquerda, E[4]);
  and and_8 (and_8_out, E[3], not_1_out);
  or or_4 (S[3], and_10_out, and_7_out);
  and and_9 (and_9_out, Direita_Esquerda, E[3]);
  and and_10 (and_10_out, E[2], not_1_out);
  and and_11 (and_11_out, Direita_Esquerda, E[2]);
  or or_5 (S[2], and_12_out, and_9_out);
  and and_12 (and_12_out, E[1], not_1_out);
  and and_13 (S[0], Direita_Esquerda, E[1]);
  or or_6 (S[1], and_14_out, and_11_out);
  and and_14 (and_14_out, E[0], not_1_out);
endmodule
