// Digital circuit subtrator.dig as structural Verilog
module subtrator (
  input  B,
  input  A,
  input  B_2,
  input  A_2,
  input  B_3,
  input  A_3,
  input  C,
  input  B_4,
  input  A_4,
  input  C_2,
  output Sb,
  output Ts,
  output So,
  output V,
  output So_2,
  output V_2,
  output Sb_2,
  output Ts_2
);

  wire and_3_out, and_4_out, and_5_out, and_6_out, and_7_out, and_8_out, not_1_out, not_2_out, not_3_out,
       xor_3_out, xor_4_out;

  not not_1 (not_1_out, A);
  xor xor_1 (So, A_2, B_2);
  and and_1 (V, B_2, A_2);
  xor xor_2 (Sb, A, B);
  and and_2 (Ts, B, not_1_out);
  not not_2 (not_2_out, A_4);
  not not_3 (not_3_out, A_4);
  xor xor_3 (xor_3_out, A_3, B_3);
  and and_3 (and_3_out, C, B_3);
  and and_4 (and_4_out, A_3, C);
  and and_5 (and_5_out, A_3, B_3);
  xor xor_4 (xor_4_out, A_4, B_4);
  and and_6 (and_6_out, C_2, B_4);
  and and_7 (and_7_out, not_2_out, C_2);
  and and_8 (and_8_out, not_3_out, B_4);
  xor xor_5 (So_2, xor_3_out, C);
  or or_1 (V_2, and_3_out, and_4_out, and_5_out);
  xor xor_6 (Sb_2, xor_4_out, C_2);
  or or_2 (Ts_2, and_6_out, and_7_out, and_8_out);

  // Notes on the sheet:
  //   Meio Somador
  //   Meio Subtrator
  //   S = A exclusivo B
  //   Ts = ~A . B
endmodule
