// Digital circuit subtrator1bit.dig as structural Verilog
module subtrator1bit (
  input  B,
  input  A,
  input  C,
  output Sb,
  output Ts
);

  wire and_1_out, and_2_out, and_3_out, not_1_out, not_2_out, xor_1_out;

  not not_1 (not_1_out, A);
  not not_2 (not_2_out, A);
  xor xor_1 (xor_1_out, A, B);
  and and_1 (and_1_out, C, B);
  and and_2 (and_2_out, not_1_out, C);
  and and_3 (and_3_out, not_2_out, B);
  xor xor_2 (Sb, xor_1_out, C);
  or or_1 (Ts, and_1_out, and_2_out, and_3_out);
endmodule
