// Digital circuit ALUc.dig as structural Verilog
module ALUc (
  input  B2,
  input  B1,
  input  B3,
  input  [7:0] B,
  input  [7:0] A,
  input  Shift_Left__Rigth,
  input  [7:0] ndaa,
  input  [7:0] nda,
  output Of,
  output [7:0] _0_7,
  output Of2
);

  wire [7:0] and8bits_1_s, or8bits_1_s, shiftleftright_1_s, somador8bits_1_s, subtrator8bits_1_s,
       xor8bits_1_p3;

  somador8bits somador8bits_1 (.A(A), .B(B), .OVERFLOW(Of), .S(somador8bits_1_s));
  Subtrator8bits subtrator8bits_1 (.A(A), .B(B), .OVERFLOW(Of2), .S(subtrator8bits_1_s));
  AND8bits and8bits_1 (.A(A), .B(B), .S(and8bits_1_s));
  // xor8bits xor8bits_1: pin names not known; wires that end beside it: A, B, xor8bits_1_p3
  Or8bits or8bits_1 (.A(A), .B(B), .S(or8bits_1_s));
  shiftLeftRight shiftleftright_1 (.Direita_Esquerda(Shift_Left__Rigth), .E(B), .S(shiftleftright_1_s));
  Multiplexer #(.Selector_Bits(3), .Bits(8)) multiplexer_1 (
    .sel({B3, B2, B1}), .in_0(somador8bits_1_s), .in_1(subtrator8bits_1_s), .in_2(and8bits_1_s),
    .in_3(xor8bits_1_p3), .in_4(or8bits_1_s), .in_5(shiftleftright_1_s), .in_6(nda), .in_7(ndaa), .out(_0_7));
endmodule
