// Digital circuit meioSomador.dig as structural Verilog
module meioSomador (
  input  B,
  input  A,
  output So,
  output V
);

  xor xor_1 (So, A, B);
  and and_1 (V, B, A);

  // Notes on the sheet:
  //   Meio Somador
endmodule
