// Digital circuit somador4bits.dig as structural Verilog
module somador4bits (
  input  in_1,
  input  in_2,
  input  in_3,
  input  in_4,
  input  in_5,
  input  in_6,
  input  in_7,
  input  in_8,
  output out_9,
  output out_10,
  output out_11,
  output out_12,
  output out_13
);

  wire somador1bit_2_v, somador1bit_3_v, somador1bit_4_v;

  somador1bit somador1bit_1 (.B(in_8), .A(in_2), .C(somador1bit_2_v), .S(out_9), .V(out_13));
  somador1bit somador1bit_2 (.B(in_5), .A(in_1), .C(somador1bit_3_v), .S(out_10), .V(somador1bit_2_v));
  somador1bit somador1bit_3 (.B(in_4), .A(in_3), .C(somador1bit_4_v), .S(out_11), .V(somador1bit_3_v));
  somador1bit somador1bit_4 (.B(in_6), .A(in_7), .C(1'b0), .S(out_12), .V(somador1bit_4_v));

  // Notes on the sheet:
  //   A
  //   B
endmodule
