// Digital circuit somador8bits.dig as structural Verilog
module somador8bits (
  input  [7:0] A,
  input  [7:0] B,
  output OVERFLOW,
  output [7:0] S
);

  wire somador_1_bit_2_v, somador_1_bit_3_v, somador_1_bit_4_v, somador_1_bit_5_v, somador_1_bit_6_v,
       somador_1_bit_7_v, somador_1_bit_8_v;

  Somador_1_bit somador_1_bit_1 (.B(B[7]), .A(A[7]), .C(somador_1_bit_2_v), .So(S[7]), .V(OVERFLOW));
  Somador_1_bit somador_1_bit_2 (.B(B[6]), .A(A[6]), .C(somador_1_bit_3_v), .So(S[6]), .V(somador_1_bit_2_v));
  Somador_1_bit somador_1_bit_3 (.B(B[5]), .A(A[5]), .C(somador_1_bit_4_v), .So(S[5]), .V(somador_1_bit_3_v));
  Somador_1_bit somador_1_bit_4 (.B(B[4]), .A(A[4]), .C(somador_1_bit_5_v), .So(S[4]), .V(somador_1_bit_4_v));
  Somador_1_bit somador_1_bit_5 (.B(B[3]), .A(A[3]), .C(somador_1_bit_6_v), .So(S[3]), .V(somador_1_bit_5_v));
  Somador_1_bit somador_1_bit_6 (.B(B[2]), .A(A[2]), .C(somador_1_bit_7_v), .So(S[2]), .V(somador_1_bit_6_v));
  Somador_1_bit somador_1_bit_7 (.B(B[1]), .A(A[1]), .C(somador_1_bit_8_v), .So(S[1]), .V(somador_1_bit_7_v));
  Somador_1_bit somador_1_bit_8 (.B(B[0]), .A(A[0]), .C(1'b0), .So(S[0]), .V(somador_1_bit_8_v));
endmodule
