// Digital circuit somador8bitsDisplay.dig as structural Verilog
module somador8bitsDisplay (
  input  in_1,
  input  in_2,
  input  in_3,
  input  in_4,
  input  in_5,
  input  in_6,
  input  in_7,
  input  in_8,
  input  in_9,
  input  in_10,
  input  in_11,
  input  in_12,
  input  in_13,
  input  in_14,
  input  in_15,
  input  in_16,
  output Overflow
);

  wire somador1bit_2_v, somador1bit_3_v, somador1bit_4_v, somador1bit_5_v, somador1bit_6_v, somador1bit_7_v,
       somador1bit_8_v;
  wire [3:0] somador1bit_1_s, somador1bit_5_s;

  somador1bit somador1bit_1 (.B(in_10), .A(in_2), .C(somador1bit_2_v), .S(somador1bit_1_s[3]), .V(Overflow));
  somador1bit somador1bit_2 (.B(in_9), .A(in_1), .C(somador1bit_3_v), .S(somador1bit_1_s[2]), .V(somador1bit_2_v));
  somador1bit somador1bit_3 (.B(in_11), .A(in_3), .C(somador1bit_4_v), .S(somador1bit_1_s[1]), .V(somador1bit_3_v));
  somador1bit somador1bit_4 (.B(in_15), .A(in_7), .C(somador1bit_5_v), .S(somador1bit_1_s[0]), .V(somador1bit_4_v));
  Seven_Seg_Hex seven_seg_hex_1 (.d(somador1bit_1_s), .dp(1'b0));
  Seven_Seg_Hex seven_seg_hex_2 (.d(somador1bit_5_s), .dp(1'b0));
  somador1bit somador1bit_5 (.B(in_16), .A(in_8), .C(somador1bit_6_v), .S(somador1bit_5_s[2]), .V(somador1bit_5_v));
  somador1bit somador1bit_6 (.B(in_13), .A(in_5), .C(somador1bit_7_v), .S(somador1bit_5_s[3]), .V(somador1bit_6_v));
  somador1bit somador1bit_7 (.B(in_12), .A(in_4), .C(somador1bit_8_v), .S(somador1bit_5_s[1]), .V(somador1bit_7_v));
  somador1bit somador1bit_8 (.B(in_14), .A(in_6), .C(1'b0), .S(somador1bit_5_s[0]), .V(somador1bit_8_v));
endmodule
